# Fritzing sketch Weather_Schematics (saved by Fritzing 0.9.3b)
circuit board: 8.46667cm x 5.64444cm

parts:
  Part1 = Photon
  7_Segment_4_Digit_Display2 = 7-SEGMENT-4DIGIT common anode [part_number="5461BS - 5462BS" package=7-segment-4digit-anode]
  R4 = Resistor [tolerance=±5% resistance=220 package=THT]
  R5 = Resistor [tolerance=±5% resistance=220 package=THT]
  R6 = Resistor [tolerance=±5% resistance=220 package=THT]
  R7 = Resistor [tolerance=±5% resistance=220 package=THT]
  Q1 = TRANSISTOR_NPN [package=to-92-ammo]
  Q2 = TRANSISTOR_NPN [package=to-92-ammo]
  Q3 = TRANSISTOR_NPN [package=to-92-ammo]
  Q4 = TRANSISTOR_NPN [package=to-92-ammo]

nets:
  N1: Part1.A0, 7_Segment_4_Digit_Display2.pin_11
  N2: Part1.A1, 7_Segment_4_Digit_Display2.pin_10
  N3: Part1.A3, R7.Pin_1
  N4: Part1.A4, R6.Pin_1
  N5: Part1.D0, 7_Segment_4_Digit_Display2.pin_1
  N6: Part1.D1, 7_Segment_4_Digit_Display2.pin_2
  N7: Part1.D2, 7_Segment_4_Digit_Display2.pin_4
  N8: Part1.D3, 7_Segment_4_Digit_Display2.pin_5
  N9: Part1.D4, 7_Segment_4_Digit_Display2.pin_7
  N10: Part1.D5, R4.Pin_0
  N11: Part1.D6, R5.Pin_0
  N12: Part1.3V3, Q1.E, Q2.E, Q3.E, Q4.E
  N13: 7_Segment_4_Digit_Display2.pin_6, Q4.C
  N14: 7_Segment_4_Digit_Display2.pin_8, Q3.C
  N15: 7_Segment_4_Digit_Display2.pin_9, Q2.C
  N16: 7_Segment_4_Digit_Display2.pin_12, Q1.C
  N17: R4.Pin_1, Q3.B
  N18: R5.Pin_1, Q4.B
  N19: R6.Pin_0, Q2.B
  N20: R7.Pin_0, Q1.B

custom parts:
  7-SEGMENT-4DIGIT common anode: A 7 Segment 4 Digit common anode display, with decimal points

// code stored in the sketch: photon-analog.ino
        
void setup(){
    pinMode(A0,INPUT);
}
void loop() {
  // Get some data
 //int temp=10;
 
  int value=analogRead(A0);
  String val=String(value);
 
  
  // Trigger the webhook
  Particle.publish("value", val, PRIVATE);
  // Wait 60 seconds
  delay(60000);
}
